# Fritzing sketch treadmill (saved by Fritzing 0.9.2b)
breadboards: 1

parts:
  Part1 = Arduino Uno (Rev3)
  M1 = Stepper Motor - Bipolar
  Part2 = EasyDriver_v44
  Raspberry_Pi1 = Raspberry Pi 2
  Part3 = Logic Level Converter
  JP1 = Header 4 [package=molex-1x4_lock]
  JP2 = Header 4 [package=molex-1x4_lock]
  Power_plug1 = Power plug

nets:
  N1: Part1.A0, Part3.TX_HV, JP2.3
  N2: Part1.A1, Part3.RX_HV, JP2.1
  N3: Part1.A5/SCL, Part3.HV, JP1.1
  N4: Part1.D11_PWM/MOSI, Part2.DIR
  N5: Part1.D12/MISO, Part2.STEP
  GND: Part1.GND, Part2.GND, Raspberry_Pi1.GND, Part3.GND, JP1.3, JP2.2, JP2.4, Power_plug1.GND
  N6: Part1.D2, JP1.4
  N7: Part1.D3_PWM, JP1.2
  N8: M1.A, Part2.OUT2A
  N9: M1.C, Part2.OUT2B
  N10: M1.B, Part2.OUT1A
  N11: M1.D, Part2.OUT1B
  N12: Part2.V+, Power_plug1.VCC
  N13: Raspberry_Pi1.3v3, Part3.LV
  N14: Raspberry_Pi1.GPIO17, Part3.TX_LV
  N15: Raspberry_Pi1.GPIO27, Part3.RX_LV

notes:
  12V DC
  Level Shifter
  Scan Image
  trigger
  frame clock
  + A - B
  + - + -
  +5V
  +3.5V
  Motor Driver
  Rotary Encoder
